// Logisim project SAP-1.circ as structural Verilog: 23 circuits, main circuit main
module main (
  input  [3:0] Address,
  input  [7:0] Data,
  input  RUN,
  output [3:0] out_4,
  output [3:0] out_5
);

  wire and_1_out, and_2_out, C_S_cp, C_S_ea, C_S_ep, C_S_eu, C_S_halt, C_S_nei, C_S_nla, C_S_nlb, C_S_nli,
       C_S_nlm, C_S_nlo, C_S_su, Clear_RAM_out, clock_1_out, controlled_buffer_1_out, not_1_out, not_2_out,
       RESET_out, Write_to_RAM_out;
  wire [3:0] IR_to_controller, MAR_to_ram, multiplexer_1_out, Output_Register_to_binary_display,
       Output_Register_to_binary_display_2;
  wire [7:0] Accumulator_to_add_sub, B_Register_to_add_sub;

  Button Write_to_RAM (.out(Write_to_RAM_out));
  Button Clear_RAM (.out(Clear_RAM_out));
  Multiplexer #(.width(4)) multiplexer_1 (
    .in0(Address), .in1(MAR_to_ram), .out(multiplexer_1_out), .sel(RUN));  // open: en
  program_counter PC (.Cp(C_S_cp), .nCLK(controlled_buffer_1_out), .Ep(C_S_ep), .CLR(RESET_out), .Out(out_5));
  Input_and_MAR MAR (
    .CLK(controlled_buffer_1_out), .CLR(RESET_out), .From_Bus(out_5), .nLm(C_S_nlm), .To_RAM(MAR_to_ram));
  not not_1 (not_1_out, RUN);
  and and_1 (and_1_out, ~RUN, Write_to_RAM_out);  // AND_Gate
  Controller_Sequencer C_S (
    .I7(IR_to_controller[3]), .I6(IR_to_controller[2]), .I5(IR_to_controller[1]), .I4(IR_to_controller[0]),
    .Cp(C_S_cp), .Ep(C_S_ep), .nLm(C_S_nlm), .nLi(C_S_nli), .nEi(C_S_nei), .nLa(C_S_nla), .Ea(C_S_ea),
    .Su(C_S_su), .Eu(C_S_eu), .nLb(C_S_nlb), .nLo(C_S_nlo), .HALT(C_S_halt));  // open: CLK, nCE
  RAM_part #(.addrWidth(4), .bus("separate")) ram_1 (
    .addr(multiplexer_1_out), .din(Data), .data({out_4, out_5}), .str(not_1_out), .clk(and_1_out),
    .clr(and_2_out));  // open: sel, ld
  and and_2 (and_2_out, ~RUN, Clear_RAM_out);  // AND_Gate
  Instruction_Register IR (
    .To_Controller(IR_to_controller), .CLK(controlled_buffer_1_out), .CLR(RESET_out),
    .From_Bus({out_4, out_5}), .nLi(C_S_nli), .nEi(C_S_nei), .To_Bus(out_5));
  not not_2 (not_2_out, C_S_halt);
  Clock clock_1 (.out(clock_1_out));
  assign controlled_buffer_1_out = not_2_out ? clock_1_out : 1'bz;  // Controlled_Buffer controlled_buffer_1
  Hex_Digit_Display hex_digit_display_1 (.value(Output_Register_to_binary_display_2));  // open: dp
  Button RESET (.out(RESET_out));
  Hex_Digit_Display hex_digit_display_2 (.value(Output_Register_to_binary_display));  // open: dp
  accumulator Accumulator (
    .To_Add_Sub(Accumulator_to_add_sub), .CLK(controlled_buffer_1_out), .CLR(RESET_out),
    .From_Bus({out_4, out_5}), .nLa(C_S_nla), .Ea(C_S_ea), .To_Bus({out_4, out_5}));
  Adder_Subtractor Adder_Subtractor (
    .From_B_Register(B_Register_to_add_sub), .To_Bus({out_4, out_5}),
    .From_Accumulator(Accumulator_to_add_sub), .Eu(C_S_eu), .Su(C_S_su));
  B_Register B_Register (
    .CLK(controlled_buffer_1_out), .CLR(RESET_out), .From_Bus({out_4, out_5}), .nLb(C_S_nlb),
    .To_Add_Sub(B_Register_to_add_sub));
  Output_Register Output_Register (
    .CLK(controlled_buffer_1_out), .CLR(RESET_out), .From_Bus({out_4, out_5}), .nLo(C_S_nlo),
    .To_Binary_Display({Output_Register_to_binary_display_2, Output_Register_to_binary_display}));
endmodule

module _4_bit_adder_subtractor (
  input  [3:0] a,
  input  [3:0] b,
  input  sub,
  output [3:0] sum,
  output carry_out
);

  wire full_adder_2_carry_out, full_adder_3_carry_out, full_adder_carry_out, xor_1_out, xor_2_out, xor_3_out,
       xor_4_out;

  xor xor_1 (xor_1_out, b[0], sub);
  xor xor_2 (xor_2_out, b[1], sub);
  xor xor_3 (xor_3_out, b[2], sub);
  xor xor_4 (xor_4_out, b[3], sub);
  full_adder full_adder (.a(a[0]), .b(xor_1_out), .c(sub), .sum(sum[0]), .carry_out(full_adder_carry_out));
  full_adder full_adder_2 (
    .a(a[1]), .b(xor_2_out), .c(full_adder_carry_out), .sum(sum[1]), .carry_out(full_adder_2_carry_out));
  full_adder full_adder_3 (
    .a(a[2]), .b(xor_3_out), .c(full_adder_2_carry_out), .sum(sum[2]), .carry_out(full_adder_3_carry_out));
  full_adder full_adder_4 (.a(a[3]), .b(xor_4_out), .c(full_adder_3_carry_out), .sum(sum[3]), .carry_out(carry_out));
endmodule

// FA
module full_adder (
  input  a,
  input  b,
  input  c,
  output sum,
  output carry_out
);

  wire and_1_out, and_2_out, xor_1_out, xor_2_out;

  xor xor_1 (xor_1_out, b, c);
  and and_1 (and_1_out, a, b);
  xor xor_2 (xor_2_out, a, b);
  xor xor_3 (sum, a, xor_1_out);
  and and_2 (and_2_out, xor_2_out, c);
  or or_1 (carry_out, and_1_out, and_2_out);
endmodule

module TTL_adder_subtractor (
  input  [7:0] a,
  input  [7:0] b,
  input  sub,
  output [7:0] sum,
  output carry_out
);

  wire _4_bit_adder_subtractor_carry_out, full_adder_2_carry_out, full_adder_3_carry_out,
       full_adder_carry_out, xor_1_out, xor_2_out, xor_3_out, xor_4_out;

  _4_bit_adder_subtractor _4_bit_adder_subtractor (
    .a(a[3:0]), .b(b[3:0]), .sub(sub), .sum(sum[3:0]), .carry_out(_4_bit_adder_subtractor_carry_out));
  xor xor_1 (xor_1_out, b[4], sub);
  xor xor_2 (xor_2_out, b[5], sub);
  xor xor_3 (xor_3_out, b[6], sub);
  xor xor_4 (xor_4_out, b[7], sub);
  full_adder full_adder (
    .a(a[4]), .b(xor_1_out), .c(_4_bit_adder_subtractor_carry_out), .sum(sum[4]),
    .carry_out(full_adder_carry_out));
  full_adder full_adder_2 (
    .a(a[5]), .b(xor_2_out), .c(full_adder_carry_out), .sum(sum[5]), .carry_out(full_adder_2_carry_out));
  full_adder full_adder_3 (
    .a(a[6]), .b(xor_3_out), .c(full_adder_2_carry_out), .sum(sum[6]), .carry_out(full_adder_3_carry_out));
  full_adder full_adder_4 (.a(a[7]), .b(xor_4_out), .c(full_adder_3_carry_out), .sum(sum[7]), .carry_out(carry_out));
endmodule

module Buffer_register (
  input  [3:0] X,
  input  LOAD,
  input  CLR,
  input  [3:0] in_4,
  output out_5
);

  wire and_1_out, and_2_out, clock_1_out, not_1_out, or_1_out;

  Clock clock_1 (.out(clock_1_out));
  not not_1 (not_1_out, LOAD);
  and and_1 (and_1_out, LOAD, X[3]);
  or or_1 (or_1_out, and_1_out, and_2_out);
  and and_2 (and_2_out, not_1_out, in_4[3]);
  edge_triggered_D_flip_flop edge_triggered_d_flip_flop_1 (
    .PRESET(or_1_out), .D(CLR), .CLEAR(clock_1_out), .Q(in_4[3]));  // open: Q_prime
endmodule

module D_flip_flop (
  input  D,
  input  CLK,
  input  CLEAR,
  output Q,
  output Q_prime
);

  wire and_1_out, and_2_out, nand_1_out, nand_2_out, not_1_out;

  not not_1 (not_1_out, D);
  nand nand_1 (nand_1_out, D, CLK);
  nand nand_2 (nand_2_out, CLK, not_1_out);
  and and_1 (and_1_out, CLEAR, nand_1_out);
  and and_2 (and_2_out, nand_2_out, CLEAR);
  nor nor_1 (Q, and_1_out, Q_prime);
  nor nor_2 (Q_prime, Q, and_2_out);
endmodule

module edge_triggered_D_flip_flop (
  input  PRESET,
  input  D,
  input  CLEAR,
  output Q,
  output Q_prime
);

  wire clock_1_out, nand_1_out, nand_2_out, nand_3_out, nand_4_out;

  Clock clock_1 (.out(clock_1_out));
  nand nand_1 (nand_1_out, PRESET, nand_4_out, nand_2_out);
  nand nand_2 (nand_2_out, nand_1_out, CLEAR, clock_1_out);
  nand nand_3 (nand_3_out, nand_2_out, clock_1_out, nand_4_out);
  nand nand_4 (nand_4_out, nand_3_out, D, CLEAR);
  nor nor_1 (Q, PRESET, nand_2_out, Q_prime);
  nor nor_2 (Q_prime, Q, nand_3_out, CLEAR);
endmodule

module Controlled_buffer_register (
  input  [3:0] X,
  input  LOAD,
  input  CLK,
  input  CLEAR,
  output [3:0] out_5
);

  wire and_1_out, and_2_out, and_3_out, and_4_out, and_5_out, and_6_out, and_7_out, and_8_out, not_1_out,
       or_1_out, or_2_out, or_3_out, or_4_out;

  and and_1 (and_1_out, X[3], LOAD);
  and and_2 (and_2_out, not_1_out, out_5[3]);
  or or_1 (or_1_out, and_1_out, and_2_out);
  D_Flip_Flop d_ff_1 (.clk(CLK), .D(or_1_out), .Q(out_5[3]), .preset(CLEAR));  // open: Qn, en, reset
  and and_3 (and_3_out, X[2], LOAD);
  or or_2 (or_2_out, and_3_out, and_4_out);
  and and_4 (and_4_out, not_1_out, out_5[2]);
  D_Flip_Flop d_ff_2 (.clk(CLK), .D(or_2_out), .Q(out_5[2]), .preset(CLEAR));  // open: Qn, en, reset
  and and_5 (and_5_out, X[1], LOAD);
  and and_6 (and_6_out, not_1_out, out_5[1]);
  or or_3 (or_3_out, and_5_out, and_6_out);
  D_Flip_Flop d_ff_3 (.clk(CLK), .D(or_3_out), .Q(out_5[1]), .preset(CLEAR));  // open: Qn, en, reset
  and and_7 (and_7_out, X[0], LOAD);
  or or_4 (or_4_out, and_7_out, and_8_out);
  and and_8 (and_8_out, not_1_out, out_5[0]);
  D_Flip_Flop d_ff_4 (.clk(CLK), .D(or_4_out), .Q(out_5[0]), .preset(CLEAR));  // open: Qn, en, reset
  not not_1 (not_1_out, LOAD);
endmodule

module accumulator (
  input  Ea,
  input  CLK,
  input  CLR,
  input  [7:0] From_Bus,
  input  nLa,
  output [7:0] To_Add_Sub,
  output [7:0] To_Bus
);

  wire not_1_out;
  wire [7:0] controlled_buffer_1_out;

  D_Flip_Flop D7 (.clk(CLK), .D(controlled_buffer_1_out[7]), .Q(To_Add_Sub[7]), .reset(CLR));  // open: Qn, preset, en
  D_Flip_Flop d_ff_1 (
    .clk(CLK), .D(controlled_buffer_1_out[6]), .Q(To_Add_Sub[6]), .reset(CLR));  // open: Qn, preset, en
  assign controlled_buffer_1_out = not_1_out ? From_Bus : 8'bz;  // Controlled_Buffer controlled_buffer_1
  not not_1 (not_1_out, nLa);
  D_Flip_Flop d_ff_2 (
    .clk(CLK), .D(controlled_buffer_1_out[5]), .Q(To_Add_Sub[5]), .reset(CLR));  // open: Qn, preset, en
  D_Flip_Flop d_ff_3 (
    .clk(CLK), .D(controlled_buffer_1_out[4]), .Q(To_Add_Sub[4]), .reset(CLR));  // open: Qn, preset, en
  D_Flip_Flop d_ff_4 (
    .clk(CLK), .D(controlled_buffer_1_out[3]), .Q(To_Add_Sub[3]), .reset(CLR));  // open: Qn, preset, en
  assign To_Bus = Ea ? To_Add_Sub : 8'bz;  // Controlled_Buffer controlled_buffer_2
  D_Flip_Flop d_ff_5 (
    .clk(CLK), .D(controlled_buffer_1_out[2]), .Q(To_Add_Sub[2]), .reset(CLR));  // open: Qn, preset, en
  D_Flip_Flop d_ff_6 (
    .clk(CLK), .D(controlled_buffer_1_out[1]), .Q(To_Add_Sub[1]), .reset(CLR));  // open: Qn, preset, en
  D_Flip_Flop D0 (.clk(CLK), .D(controlled_buffer_1_out[0]), .Q(To_Add_Sub[0]), .reset(CLR));  // open: Qn, preset, en
endmodule

module b_register (
  input  [7:0] X,
  input  LOAD,
  output [7:0] out_3
);

  wire clock_1_out;

  Clock clock_1 (.out(clock_1_out));
  Controlled_buffer_register controlled_buffer_register_1 (
    .X(X[7:4]), .CLK(clock_1_out), .LOAD(LOAD), .out_5(out_3[7:4]));  // open: CLEAR
  Controlled_buffer_register controlled_buffer_register_2 (
    .X(X[3:0]), .CLK(clock_1_out), .LOAD(LOAD), .out_5(out_3[3:0]));  // open: CLEAR
endmodule

module output_register (
  input  [7:0] X,
  input  LOAD,
  output [7:0] out_3
);

  wire clock_1_out;

  Clock clock_1 (.out(clock_1_out));
  Controlled_buffer_register controlled_buffer_register_1 (
    .X(X[7:4]), .CLK(clock_1_out), .LOAD(LOAD), .out_5(out_3[7:4]));  // open: CLEAR
  Controlled_buffer_register controlled_buffer_register_2 (
    .X(X[3:0]), .CLK(clock_1_out), .LOAD(LOAD), .out_5(out_3[3:0]));  // open: CLEAR
endmodule

module program_counter (
  input  Cp,
  input  nCLK,
  input  Ep,
  input  CLR,
  output [3:0] Out
);

  wire half_adder_1_sum, half_adder_2_p1, half_adder_2_p3, half_adder_2_p7, half_adder_3_p3, half_adder_3_p7,
       half_adder_4_p3, not_1_out;
  wire [3:0] half_adder_4_p8;

  not not_1 (not_1_out, nCLK);
  half_adder half_adder_1 (.A(half_adder_1_sum), .B(half_adder_1_sum), .SUM(half_adder_1_sum));  // open: CARRY
  D_Flip_Flop d_ff_1 (
    .clk(not_1_out), .D(half_adder_1_sum), .Q(half_adder_4_p8[3]), .reset(CLR));  // open: Qn, preset, en
  // half_adder half_adder_2: pin names not known; wires that end beside it: half_adder_2_p1, half_adder_4_p8[3], half_adder_2_p3, half_adder_2_p3, half_adder_2_p1, half_adder_2_p3, half_adder_2_p7, half_adder_4_p8[2]
  D_Flip_Flop d_ff_2 (
    .clk(not_1_out), .D(half_adder_2_p3), .Q(half_adder_4_p8[2]), .reset(CLR));  // open: Qn, preset, en
  // half_adder half_adder_3: pin names not known; wires that end beside it: half_adder_2_p7, half_adder_4_p8[2], half_adder_3_p3, half_adder_3_p3, half_adder_2_p7, half_adder_3_p3, half_adder_3_p7, half_adder_4_p8[1]
  D_Flip_Flop d_ff_3 (
    .clk(not_1_out), .D(half_adder_3_p3), .Q(half_adder_4_p8[1]), .reset(CLR));  // open: Qn, preset, en
  // half_adder half_adder_4: pin names not known; wires that end beside it: half_adder_3_p7, half_adder_4_p8[1], half_adder_4_p3, half_adder_4_p3, half_adder_3_p7, half_adder_4_p3, Cp, half_adder_4_p8[0]
  D_Flip_Flop d_ff_4 (
    .clk(not_1_out), .D(half_adder_4_p3), .Q(half_adder_4_p8[0]), .reset(CLR));  // open: Qn, preset, en
  assign Out = Ep ? half_adder_4_p8 : 4'bz;  // Controlled_Buffer controlled_buffer_1
endmodule

module ring_counter (
  input  CLR
);

  wire clock_1_out, d_ff_1_q, d_ff_2_q, d_ff_3_q, d_ff_4_q, not_1_out;

  D_Flip_Flop d_ff_1 (.clk(clock_1_out), .D(d_ff_2_q), .Q(d_ff_1_q), .reset(not_1_out));  // open: Qn, preset, en
  D_Flip_Flop d_ff_2 (.clk(clock_1_out), .D(d_ff_3_q), .Q(d_ff_2_q), .reset(not_1_out));  // open: Qn, preset, en
  D_Flip_Flop d_ff_3 (.clk(clock_1_out), .D(d_ff_4_q), .Q(d_ff_3_q), .reset(not_1_out));  // open: Qn, preset, en
  D_Flip_Flop d_ff_4 (.clk(clock_1_out), .D(d_ff_1_q), .Q(d_ff_4_q), .preset(not_1_out));  // open: Qn, en, reset
  not not_1 (not_1_out, CLR);
  Clock clock_1 (.out(clock_1_out));
endmodule

// HA
module half_adder (
  input  A,
  input  B,
  output SUM,
  output CARRY
);

  xor xor_1 (SUM, A, B);
  and and_1 (CARRY, A, B);
endmodule

module Input_and_MAR (
  input  CLK,
  input  CLR,
  input  [3:0] From_Bus,
  input  nLm,
  output [3:0] To_RAM
);

  wire not_1_out;
  wire [3:0] controlled_buffer_1_out;

  assign controlled_buffer_1_out = not_1_out ? From_Bus : 4'bz;  // Controlled_Buffer controlled_buffer_1
  not not_1 (not_1_out, nLm);
  D_Flip_Flop d_ff_1 (.clk(CLK), .D(controlled_buffer_1_out[3]), .Q(To_RAM[3]), .reset(CLR));  // open: Qn, preset, en
  D_Flip_Flop d_ff_2 (.clk(CLK), .D(controlled_buffer_1_out[2]), .Q(To_RAM[2]), .reset(CLR));  // open: Qn, preset, en
  D_Flip_Flop d_ff_3 (.clk(CLK), .D(controlled_buffer_1_out[1]), .Q(To_RAM[1]), .reset(CLR));  // open: Qn, preset, en
  D_Flip_Flop D0 (.clk(CLK), .D(controlled_buffer_1_out[0]), .Q(To_RAM[0]), .reset(CLR));  // open: Qn, preset, en
endmodule

module RAM (
  input  Cp,
  input  nCLK,
  input  Ep,
  input  CLR,
  output [3:0] Output_to_Bus
);

  wire half_adder_1_sum, half_adder_2_p1, half_adder_2_p3, half_adder_2_p7, half_adder_3_p3, half_adder_3_p7,
       half_adder_4_p3, not_1_out;
  wire [3:0] half_adder_4_p8;

  not not_1 (not_1_out, nCLK);
  half_adder half_adder_1 (.A(half_adder_1_sum), .B(half_adder_1_sum), .SUM(half_adder_1_sum));  // open: CARRY
  D_Flip_Flop d_ff_1 (
    .clk(not_1_out), .D(half_adder_1_sum), .Q(half_adder_4_p8[3]), .reset(CLR));  // open: Qn, preset, en
  // half_adder half_adder_2: pin names not known; wires that end beside it: half_adder_2_p1, half_adder_4_p8[3], half_adder_2_p3, half_adder_2_p3, half_adder_2_p1, half_adder_2_p3, half_adder_2_p7, half_adder_4_p8[2]
  D_Flip_Flop d_ff_2 (
    .clk(not_1_out), .D(half_adder_2_p3), .Q(half_adder_4_p8[2]), .reset(CLR));  // open: Qn, preset, en
  // half_adder half_adder_3: pin names not known; wires that end beside it: half_adder_2_p7, half_adder_4_p8[2], half_adder_3_p3, half_adder_3_p3, half_adder_2_p7, half_adder_3_p3, half_adder_3_p7, half_adder_4_p8[1]
  D_Flip_Flop d_ff_3 (
    .clk(not_1_out), .D(half_adder_3_p3), .Q(half_adder_4_p8[1]), .reset(CLR));  // open: Qn, preset, en
  // half_adder half_adder_4: pin names not known; wires that end beside it: half_adder_3_p7, half_adder_4_p8[1], half_adder_4_p3, half_adder_4_p3, half_adder_3_p7, half_adder_4_p3, Cp, half_adder_4_p8[0]
  D_Flip_Flop d_ff_4 (
    .clk(not_1_out), .D(half_adder_4_p3), .Q(half_adder_4_p8[0]), .reset(CLR));  // open: Qn, preset, en
  assign Output_to_Bus = Ep ? half_adder_4_p8 : 4'bz;  // Controlled_Buffer controlled_buffer_1
endmodule

module Instruction_Register (
  input  nEi,
  input  CLK,
  input  CLR,
  input  [7:0] From_Bus,
  input  nLi,
  output [3:0] To_Bus,
  output [3:0] To_Controller
);

  wire not_1_out, not_2_out;
  wire [3:0] D0_q;
  wire [7:0] controlled_buffer_1_out;

  not not_1 (not_1_out, nLi);
  D_Flip_Flop D7 (
    .clk(CLK), .D(controlled_buffer_1_out[7]), .Q(To_Controller[3]), .reset(CLR));  // open: Qn, preset, en
  assign controlled_buffer_1_out = not_1_out ? From_Bus : 8'bz;  // Controlled_Buffer controlled_buffer_1
  D_Flip_Flop d_ff_1 (
    .clk(CLK), .D(controlled_buffer_1_out[6]), .Q(To_Controller[2]), .reset(CLR));  // open: Qn, preset, en
  D_Flip_Flop d_ff_2 (
    .clk(CLK), .D(controlled_buffer_1_out[5]), .Q(To_Controller[1]), .reset(CLR));  // open: Qn, preset, en
  D_Flip_Flop d_ff_3 (
    .clk(CLK), .D(controlled_buffer_1_out[4]), .Q(To_Controller[0]), .reset(CLR));  // open: Qn, preset, en
  D_Flip_Flop d_ff_4 (.clk(CLK), .D(controlled_buffer_1_out[3]), .Q(D0_q[3]), .reset(CLR));  // open: Qn, preset, en
  D_Flip_Flop d_ff_5 (.clk(CLK), .D(controlled_buffer_1_out[2]), .Q(D0_q[2]), .reset(CLR));  // open: Qn, preset, en
  assign To_Bus = not_2_out ? D0_q : 4'bz;  // Controlled_Buffer controlled_buffer_2
  not not_2 (not_2_out, nEi);
  D_Flip_Flop d_ff_6 (.clk(CLK), .D(controlled_buffer_1_out[1]), .Q(D0_q[1]), .reset(CLR));  // open: Qn, preset, en
  D_Flip_Flop D0 (.clk(CLK), .D(controlled_buffer_1_out[0]), .Q(D0_q[0]), .reset(CLR));  // open: Qn, preset, en
endmodule

module Adder_Subtractor (
  input  [7:0] From_B_Register,
  input  Su,
  input  Eu,
  input  [7:0] From_Accumulator,
  output [7:0] To_Bus
);

  wire full_adder_2_carry_out, full_adder_3_carry_out, full_adder_4_carry_out, full_adder_5_carry_out,
       full_adder_6_carry_out, full_adder_7_carry_out, full_adder_8_carry_out, xor_1_out, xor_2_out,
       xor_3_out, xor_4_out, xor_5_out, xor_6_out, xor_7_out, xor_8_out;
  wire [7:0] full_adder_8_sum;

  assign To_Bus = Eu ? full_adder_8_sum : 8'bz;  // Controlled_Buffer controlled_buffer_1
  xor xor_1 (xor_1_out, Su, From_B_Register[7]);
  full_adder full_adder_1 (
    .a(From_Accumulator[7]), .b(xor_1_out), .c(full_adder_2_carry_out), .sum(full_adder_8_sum[7]));  // open: carry_out
  full_adder full_adder_2 (
    .a(From_Accumulator[6]), .b(xor_2_out), .c(full_adder_3_carry_out), .sum(full_adder_8_sum[6]),
    .carry_out(full_adder_2_carry_out));
  xor xor_2 (xor_2_out, Su, From_B_Register[6]);
  full_adder full_adder_3 (
    .a(From_Accumulator[5]), .b(xor_3_out), .c(full_adder_4_carry_out), .sum(full_adder_8_sum[5]),
    .carry_out(full_adder_3_carry_out));
  xor xor_3 (xor_3_out, Su, From_B_Register[5]);
  xor xor_4 (xor_4_out, Su, From_B_Register[4]);
  full_adder full_adder_4 (
    .a(From_Accumulator[4]), .b(xor_4_out), .c(full_adder_6_carry_out), .sum(full_adder_8_sum[4]),
    .carry_out(full_adder_4_carry_out));
  xor xor_5 (xor_5_out, Su, From_B_Register[3]);
  full_adder full_adder_5 (
    .a(From_Accumulator[2]), .b(xor_6_out), .c(full_adder_7_carry_out), .sum(full_adder_8_sum[2]),
    .carry_out(full_adder_5_carry_out));
  full_adder full_adder_6 (
    .a(From_Accumulator[3]), .b(xor_5_out), .c(full_adder_5_carry_out), .sum(full_adder_8_sum[3]),
    .carry_out(full_adder_6_carry_out));
  xor xor_6 (xor_6_out, Su, From_B_Register[2]);
  full_adder full_adder_7 (
    .a(From_Accumulator[1]), .b(xor_7_out), .c(full_adder_8_carry_out), .sum(full_adder_8_sum[1]),
    .carry_out(full_adder_7_carry_out));
  xor xor_7 (xor_7_out, Su, From_B_Register[1]);
  xor xor_8 (xor_8_out, Su, From_B_Register[0]);
  full_adder full_adder_8 (
    .a(From_Accumulator[0]), .b(xor_8_out), .c(Su), .sum(full_adder_8_sum[0]),
    .carry_out(full_adder_8_carry_out));
endmodule

module B_Register (
  input  CLK,
  input  CLR,
  input  [7:0] From_Bus,
  input  nLb,
  output [7:0] To_Add_Sub
);

  wire not_1_out;
  wire [7:0] controlled_buffer_1_out;

  D_Flip_Flop D7 (.clk(CLK), .D(controlled_buffer_1_out[7]), .Q(To_Add_Sub[7]), .reset(CLR));  // open: Qn, preset, en
  D_Flip_Flop d_ff_1 (
    .clk(CLK), .D(controlled_buffer_1_out[6]), .Q(To_Add_Sub[6]), .reset(CLR));  // open: Qn, preset, en
  assign controlled_buffer_1_out = not_1_out ? From_Bus : 8'bz;  // Controlled_Buffer controlled_buffer_1
  not not_1 (not_1_out, nLb);
  D_Flip_Flop d_ff_2 (
    .clk(CLK), .D(controlled_buffer_1_out[5]), .Q(To_Add_Sub[5]), .reset(CLR));  // open: Qn, preset, en
  D_Flip_Flop d_ff_3 (
    .clk(CLK), .D(controlled_buffer_1_out[4]), .Q(To_Add_Sub[4]), .reset(CLR));  // open: Qn, preset, en
  D_Flip_Flop d_ff_4 (
    .clk(CLK), .D(controlled_buffer_1_out[3]), .Q(To_Add_Sub[3]), .reset(CLR));  // open: Qn, preset, en
  D_Flip_Flop d_ff_5 (
    .clk(CLK), .D(controlled_buffer_1_out[2]), .Q(To_Add_Sub[2]), .reset(CLR));  // open: Qn, preset, en
  D_Flip_Flop d_ff_6 (
    .clk(CLK), .D(controlled_buffer_1_out[1]), .Q(To_Add_Sub[1]), .reset(CLR));  // open: Qn, preset, en
  D_Flip_Flop D0 (.clk(CLK), .D(controlled_buffer_1_out[0]), .Q(To_Add_Sub[0]), .reset(CLR));  // open: Qn, preset, en
endmodule

module Output_Register (
  input  CLK,
  input  CLR,
  input  [7:0] From_Bus,
  input  nLo,
  output [7:0] To_Binary_Display
);

  wire not_1_out;
  wire [7:0] controlled_buffer_1_out;

  D_Flip_Flop D7 (
    .clk(CLK), .D(controlled_buffer_1_out[7]), .Q(To_Binary_Display[7]), .reset(CLR));  // open: Qn, preset, en
  D_Flip_Flop d_ff_1 (
    .clk(CLK), .D(controlled_buffer_1_out[6]), .Q(To_Binary_Display[6]), .reset(CLR));  // open: Qn, preset, en
  assign controlled_buffer_1_out = not_1_out ? From_Bus : 8'bz;  // Controlled_Buffer controlled_buffer_1
  not not_1 (not_1_out, nLo);
  D_Flip_Flop d_ff_2 (
    .clk(CLK), .D(controlled_buffer_1_out[5]), .Q(To_Binary_Display[5]), .reset(CLR));  // open: Qn, preset, en
  D_Flip_Flop d_ff_3 (
    .clk(CLK), .D(controlled_buffer_1_out[4]), .Q(To_Binary_Display[4]), .reset(CLR));  // open: Qn, preset, en
  D_Flip_Flop d_ff_4 (
    .clk(CLK), .D(controlled_buffer_1_out[3]), .Q(To_Binary_Display[3]), .reset(CLR));  // open: Qn, preset, en
  D_Flip_Flop d_ff_5 (
    .clk(CLK), .D(controlled_buffer_1_out[2]), .Q(To_Binary_Display[2]), .reset(CLR));  // open: Qn, preset, en
  D_Flip_Flop d_ff_6 (
    .clk(CLK), .D(controlled_buffer_1_out[1]), .Q(To_Binary_Display[1]), .reset(CLR));  // open: Qn, preset, en
  D_Flip_Flop D0 (
    .clk(CLK), .D(controlled_buffer_1_out[0]), .Q(To_Binary_Display[0]), .reset(CLR));  // open: Qn, preset, en
endmodule

module Controller_Sequencer (
  input  CLK,
  input  I7,
  input  I6,
  input  I5,
  input  I4,
  output Cp,
  output Ep,
  output nLm,
  output nCE,
  output nLi,
  output nEi,
  output nLa,
  output Ea,
  output Su,
  output Eu,
  output nLb,
  output nLo,
  output HALT
);

  wire and_1_out, and_2_out, and_3_out, and_4_out, and_5_out, and_6_out, and_7_out, and_8_out, and_9_out,
       and_10_out, and_11_out, and_12_out, and_15_out, and_16_out, and_17_out, and_18_out,
       Instruction_Decoder_add, Instruction_Decoder_lda, Instruction_Decoder_out, Instruction_Decoder_sub,
       Ring_Counter_t3, Ring_Counter_t4, Ring_Counter_t5, Ring_Counter_t6;

  Instruction_Decoder Instruction_Decoder (
    .I7(I7), .I6(I6), .I5(I5), .I4(I4), .LDA(Instruction_Decoder_lda), .ADD(Instruction_Decoder_add),
    .SUB(Instruction_Decoder_sub), .OUT(Instruction_Decoder_out), .HLT(HALT));
  Ring_Counter Ring_Counter (
    .CLK(CLK), .T1(Ep), .T2(Cp), .T3(Ring_Counter_t3), .T4(Ring_Counter_t4), .T5(Ring_Counter_t5),
    .T6(Ring_Counter_t6));
  and and_1 (and_1_out, Ring_Counter_t4, Instruction_Decoder_lda);
  and and_2 (and_2_out, Ring_Counter_t4, Instruction_Decoder_sub);
  and and_3 (and_3_out, Ring_Counter_t4, Instruction_Decoder_add);
  nor nor_1 (nLm, and_1_out, and_3_out, and_2_out, Ep);
  and and_4 (and_4_out, Ring_Counter_t5, Instruction_Decoder_lda);
  and and_5 (and_5_out, Ring_Counter_t5, Instruction_Decoder_add);
  and and_6 (and_6_out, Ring_Counter_t5, Instruction_Decoder_sub);
  nor nor_2 (nCE, and_4_out, and_5_out, and_6_out, Ring_Counter_t3);
  not not_1 (nLi, Ring_Counter_t3);
  and and_7 (and_7_out, Ring_Counter_t4, Instruction_Decoder_add);
  and and_8 (and_8_out, Ring_Counter_t4, Instruction_Decoder_lda);
  nor nor_3 (nEi, and_8_out, and_7_out, and_9_out);
  and and_9 (and_9_out, Ring_Counter_t4, Instruction_Decoder_sub);
  and and_10 (and_10_out, Ring_Counter_t5, Instruction_Decoder_lda);
  and and_11 (and_11_out, Instruction_Decoder_add, Ring_Counter_t6);
  and and_12 (and_12_out, Ring_Counter_t6, Instruction_Decoder_sub);
  nor nor_4 (nLa, and_10_out, and_11_out, and_12_out);
  and and_13 (Ea, Ring_Counter_t4, Instruction_Decoder_out);
  and and_14 (Su, Ring_Counter_t6, Instruction_Decoder_sub);
  and and_15 (and_15_out, Ring_Counter_t6, Instruction_Decoder_sub);
  and and_16 (and_16_out, Ring_Counter_t6, Instruction_Decoder_add);
  or or_1 (Eu, and_16_out, and_15_out);
  and and_17 (and_17_out, Instruction_Decoder_add, Ring_Counter_t5);
  and and_18 (and_18_out, Ring_Counter_t5, Instruction_Decoder_sub);
  nor nor_5 (nLb, and_17_out, and_18_out);
  nand nand_1 (nLo, Instruction_Decoder_out, Ring_Counter_t4);
endmodule

module Ring_Counter (
  input  CLK,
  output T1,
  output T2,
  output T3,
  output T4,
  output T5,
  output T6
);

  wire nor_1_out;

  nor nor_1 (nor_1_out, T1, T2, T3, T4, T5, T6);
  D_Flip_Flop D1 (.clk(CLK), .D(nor_1_out), .Q(T1));  // open: Qn, preset, en, reset
  D_Flip_Flop d_ff_1 (.clk(CLK), .D(T1), .Q(T2));  // open: Qn, preset, en, reset
  D_Flip_Flop d_ff_2 (.clk(CLK), .D(T2), .Q(T3));  // open: Qn, preset, en, reset
  D_Flip_Flop d_ff_3 (.clk(CLK), .D(T3), .Q(T4));  // open: Qn, preset, en, reset
  D_Flip_Flop d_ff_4 (.clk(CLK), .D(T4), .Q(T5));  // open: Qn, preset, en, reset
  D_Flip_Flop d_ff_5 (.clk(CLK), .D(T5), .Q(T6));  // open: Qn, preset, en, reset
endmodule

module Instruction_Decoder (
  input  I7,
  input  I6,
  input  I5,
  input  I4,
  output LDA,
  output ADD,
  output SUB,
  output OUT,
  output HLT
);

  wire not_1_out, not_2_out, not_3_out, not_4_out;

  not not_1 (not_1_out, I7);
  not not_2 (not_2_out, I6);
  not not_3 (not_3_out, I5);
  not not_4 (not_4_out, I4);
  and and_1 (LDA, I7, not_2_out, I5, I4);
  and and_2 (ADD, not_1_out, I6, not_3_out, I4);
  and and_3 (SUB, not_1_out, I6, I5, I4);
  and and_4 (OUT, not_1_out, not_2_out, not_3_out, not_4_out);
  and and_5 (HLT, not_1_out, I6, not_3_out, not_4_out);
endmodule
